# Fritzing sketch Arduino_DS18B20_CP2101 (saved by Fritzing 0.9.3b)
breadboards: 1

parts:
  Part1 = Arduino Nano (Rev3.0)
  DS1 = DS18B20 1-Wire Temperature Sensor [part_number=DS18B20]
  R1 = Resistor [tolerance=±5% resistance=4.7k package="0402 [SMD]"]
  X1 = USB Connectors [package=usb-a-h]

nets:
  N1: Part1.D1/TX, X1.VBUS
  N2: Part1.D0/RX, X1.GND
  GND: Part1.GND, DS1.GND, X1.D+
  N3: Part1.D9, DS1.DQ, R1.Pin_1
  5V: Part1.5V, DS1.VDD, R1.Pin_0

notes:
  CP2102 GND,RX,TX
